// Logisim project LogisimProjekt.circ as structural Verilog: 1 circuit, main circuit main
module main (
  input  A,
  input  B,
  input  C,
  input  D,
  output Y_zadanie,
  output Z_zadanie,
  output Y_DNF,
  output Z_DNF,
  output Z_KNF,
  output Y_KNF
);

  wire A_B_C_out, A_B_nD_out, A_D_out, A_nC_out, B_D_2_out, B_D_out, B_nC_out, n_A_B_out, n_C_nD_out,
       nA_nB_C_nD_out, nA_nC_D_out, nA_out, nB_nC_D_out, not_1_out, not_2_out, not_3_out, not_4_out,
       not_5_out, not_6_out, not_7_out, not_8_out;

  not not_1 (not_1_out, D);
  not not_2 (not_2_out, C);
  not nA (nA_out, A);
  not not_3 (not_3_out, B);
  not not_4 (not_4_out, D);
  not not_5 (not_5_out, D);
  not not_6 (not_6_out, A);
  not not_7 (not_7_out, C);
  not not_8 (not_8_out, B);
  nor n_A_B (n_A_B_out, A, B);
  nand n_C_nD (n_C_nD_out, C, not_1_out);
  or B_D (B_D_out, B, D);
  and A_nC (A_nC_out, A, not_2_out);
  and A_D (A_D_out, A, D);
  and B_nC (B_nC_out, B, not_2_out);
  and B_D_2 (B_D_2_out, B, D);
  and nA_nB_C_nD (nA_nB_C_nD_out, nA_out, not_3_out, C, not_4_out);
  and nB_C_nD (Z_DNF, not_4_out, C, C, not_3_out);
  and nB_C_nD_2 (Z_KNF, not_3_out, not_4_out, C);
  or A_B_C (A_B_C_out, A, B, C);
  or A_B_nD (A_B_nD_out, A, B, not_5_out);
  or nA_nC_D (nA_nC_D_out, not_6_out, D, not_7_out);
  or nB_nC_D (nB_nC_D_out, not_7_out, not_8_out, D);
  xor nn_A_B__n_C_nD__nn_C_nD__n_A_B (Y_zadanie, n_A_B_out, n_C_nD_out);
  nor n__B_D__n_C_nD (Z_zadanie, n_C_nD_out, B_D_out);
  and A_B_C___A_B_nD___nA_nC_D___nB_nC_D (Y_KNF, A_B_C_out, A_B_nD_out, nA_nC_D_out, nB_nC_D_out);
  or A_nC_A_D_B_nC_B_D_nA_nB_C_nD (Y_DNF, A_nC_out, A_D_out, B_nC_out, B_D_2_out, nA_nB_C_nD_out);

  // Notes on the sheet:
  //   DNF
  //   ZADANIE
  //   !D
  //   !C
  //   !B
  //   !D
  //   !D
  //   !A
  //   !C
  //   !B
  //   KNF
endmodule
