// Logisim project Zadanie2.circ as structural Verilog: 1 circuit, main circuit main
module main (
  input  a,
  input  b,
  input  c,
  input  d,
  output A_D,
  output B_D,
  output C_D,
  output D_D,
  output E_D,
  output A_K,
  output B_K,
  output C_K,
  output D_K,
  output E_K
);

  wire a_b_c_out, a_c_nd_out, a_d_c_out, a_d_out, a_nb_nd_out, b_d_nc_out, b_d_out, b_nc_out, c_a_nd_out,
       c_na_out, c_nd_out, d_c_na_out, d_nc_out, nb_d_c_out, nb_nc_nd_out, nb_nd_nc_out, nc___a_out,
       nc_b_d_out, nc_d_a_out, nc_nb_d_out, nd___na___b_out, not_1_out, not_2_out, not_3_out, not_4_out,
       not_5_out, not_6_out, not_7_out, not_8_out;

  not not_1 (not_1_out, a);
  not not_2 (not_2_out, a);
  not not_3 (not_3_out, b);
  not not_4 (not_4_out, b);
  not not_5 (not_5_out, c);
  not not_6 (not_6_out, c);
  not not_7 (not_7_out, d);
  not not_8 (not_8_out, d);
  and u_a_d (a_d_out, a, d);
  and c_na (c_na_out, not_1_out, c);
  and a_b_c (a_b_c_out, a, b, c);
  and c_nd (c_nd_out, c, not_7_out);
  and b_nc (b_nc_out, b, not_5_out);
  and u_b_d (b_d_out, b, d);
  and d_nc (d_nc_out, d, not_5_out);
  and a_nb_nd (a_nb_nd_out, a, not_3_out, not_7_out);
  and nb_nc_nd (nb_nc_nd_out, not_3_out, not_5_out, not_7_out);
  and b_d_nc (b_d_nc_out, b, d, not_5_out);
  and d_c_na (d_c_na_out, d, c, not_1_out);
  and a_c_nd (a_c_nd_out, a, c, not_7_out);
  or nc_b_d (nc_b_d_out, not_6_out, b, d);
  or nd___na___b (nd___na___b_out, not_8_out, not_2_out, b);
  or a_d_c (a_d_c_out, a, d, c);
  or nc___a (nc___a_out, not_6_out, a);
  or nc_nb_d (nc_nb_d_out, not_6_out, not_4_out, d);
  or nb_d_c (nb_d_c_out, not_4_out, d, c);
  or nb_nd_nc (nb_nd_nc_out, not_4_out, not_6_out, not_8_out);
  or nc_d_a (nc_d_a_out, not_6_out, d, a);
  or c_a_nd (c_a_nd_out, c, a, not_8_out);
  and a__nc_b_d (A_K, a, nc_b_d_out);
  and c__nd_na_b (B_K, nd___na___b_out, c);
  or b_a_d (A_D, b, a_d_out);
  or c_na___a_b_c___c_nd (B_D, c_na_out, a_b_c_out, c_nd_out);
  or b_nc___b_d___d_nc___a_nb_nd (C_D, b_nc_out, b_d_out, d_nc_out, a_nb_nd_out);
  or nb_nc_nd___b_d_nc___d_c_na___a_c_nd (D_D, nb_nc_nd_out, b_d_nc_out, d_c_na_out, a_c_nd_out);
  and nb_d_c___nb_nd_nc___nc_d_a___na_nd_b___c_a_d (D_K, nd___na___b_out, nb_d_c_out, nb_nd_nc_out, nc_d_a_out, c_a_nd_out);
  and a_d_c___nc_a___nd_na_b___nc_nb_d (C_K, nd___na___b_out, a_d_c_out, nc___a_out, nc_nb_d_out);

  assign E_D = d;
  assign E_K = d;

  // Notes on the sheet:
  //   !a
  //   !b
  //   !c
  //   !d
endmodule
