// Logisim project Zadanie3 (1).circ as structural Verilog: 1 circuit, main circuit main
module main (
  input  X,
  input  reset,
  output Y
);

  wire clock_1_out, j_k_ff_1_q, j_k_ff_1_qn, j_k_ff_2_q, j_k_ff_2_qn, j_k_ff_3_q, j_k_ff_3_qn, n_Z2_X_out,
       n_Z3_nX_nZ2_out, n_Z3_nX_out, nX_out, X_nZ3_out, Z1_Z2_Z3_nX_out, Z2_nX___Z2_X_nZ1_Z3_nX_nZ1_out,
       Z2_nX_out, Z2_X_nZ1_nX_out, Z2_X_nZ1_out, Z2_X_out, Z3_nX_nZ1_out, Z3_nX_nZ2_out, Z3_nX_out;

  not nX (nX_out, X);  // NAND_Gate
  Clock clock_1 (.out(clock_1_out));
  nand Z2_X (Z2_X_out, X, j_k_ff_2_q);
  nand Z3_nX_nZ2 (Z3_nX_nZ2_out, j_k_ff_3_q, nX_out, j_k_ff_2_qn);
  nand Z3_nX (Z3_nX_out, nX_out, j_k_ff_3_q);
  nand X_nZ3 (X_nZ3_out, X, j_k_ff_3_qn);
  nand Z2_X_nZ1 (Z2_X_nZ1_out, j_k_ff_2_q, X, j_k_ff_1_qn);
  nand Z2_nX (Z2_nX_out, j_k_ff_2_q, nX_out);
  and Z3_nX_nZ1 (Z3_nX_nZ1_out, j_k_ff_3_q, nX_out, j_k_ff_1_qn);
  nand n_Z2_X (n_Z2_X_out, Z2_X_out, Z2_X_out);
  nand n_Z3_nX_nZ2 (n_Z3_nX_nZ2_out, Z3_nX_nZ2_out, Z3_nX_nZ2_out);
  nand n_Z3_nX (n_Z3_nX_out, Z3_nX_out, Z3_nX_out);
  nand n_X_nZ3 (clock_1_out, X_nZ3_out, X_nZ3_out);
  nand Z2_X_nZ1_nX (Z2_X_nZ1_nX_out, Z2_X_nZ1_out, nX_out);
  nand Z2_nX___Z2_X_nZ1_Z3_nX_nZ1 (Z2_nX___Z2_X_nZ1_Z3_nX_nZ1_out, Z2_X_nZ1_out, Z2_nX_out, Z3_nX_nZ1_out);
  nand Z1_Z2_Z3_nX (Z1_Z2_Z3_nX_out, j_k_ff_1_q, nX_out, j_k_ff_2_q, j_k_ff_3_q);
  nand n_Z1_Z2_Z3_nX (Y, Z1_Z2_Z3_nX_out, Z1_Z2_Z3_nX_out);
  J_K_Flip_Flop j_k_ff_1 (
    .J(n_Z2_X_out), .clk(clock_1_out), .K(n_Z3_nX_nZ2_out), .Q(j_k_ff_1_q), .Qn(j_k_ff_1_qn), .reset(reset));  // open: preset, en
  J_K_Flip_Flop j_k_ff_2 (
    .J(n_Z3_nX_out), .clk(clock_1_out), .K(clock_1_out), .Q(j_k_ff_2_q), .Qn(j_k_ff_2_qn), .reset(reset));  // open: preset, en
  J_K_Flip_Flop j_k_ff_3 (
    .J(Z2_X_nZ1_nX_out), .clk(clock_1_out), .K(Z2_nX___Z2_X_nZ1_Z3_nX_nZ1_out), .Q(j_k_ff_3_q),
    .Qn(j_k_ff_3_qn), .reset(reset));  // open: preset, en

  // Notes on the sheet:
  //   Z1
  //   !Z1
  //   Z2
  //   !Z2
  //   Z3
  //   !Z3
  //   J1
  //   K1
  //   J2
  //   K2
  //   J3
endmodule
